// Logisim project part3.circ as structural Verilog: 1 circuit, main circuit main
module main (
  input  D,
  output Q,
  output Qn
);

  wire CLK_out, d_ff_1_q, not_1_out, not_2_out;

  Clock CLK (.out(CLK_out));
  not not_1 (not_1_out, CLK_out);
  D_Flip_Flop d_ff_1 (.D(D), .Q(d_ff_1_q), .en(not_1_out));  // open: clk, Qn, preset, reset
  D_Flip_Flop d_ff_2 (.D(d_ff_1_q), .Q(Q), .Qn(Qn), .en(not_2_out));  // open: clk, preset, reset
  not not_2 (not_2_out, not_1_out);

  // Notes on the sheet:
  //   E
  //   Qm
  //   E
endmodule
